// Logisim project ВвКиВТ.circ as structural Verilog
module \_1_лаба  (
  output out_1,
  output out_2,
  output out_3,
  output out_4,
  output out_5,
  output out_6,
  output out_7,
  output out_8,
  output out_9,
  output out_10,
  output out_11
);

  wire transistor_2_out, transistor_7_out, transistor_11_out, transistor_16_out, transistor_20_out;

  Transistor #(.\type ("n")) transistor_1 (.in(1'b0), .out(out_6), .gate(1'b1));
  Transistor transistor_2 (.in(1'b1), .out(transistor_2_out), .gate(1'b1));
  Transistor transistor_3 (.in(transistor_2_out), .out(out_6), .gate(1'b1));
  Transistor #(.\type ("n")) transistor_4 (.in(1'b0), .out(out_6), .gate(1'b1));
  Transistor transistor_5 (.in(1'b1), .out(out_3), .gate(1'b0));
  not not_1 (out_4, 1'b1);
  nor nor_1 (out_9, 1'b1, 1'b1);
  Transistor #(.\type ("n")) transistor_6 (.in(1'b0), .out(out_3), .gate(1'b0));
  Transistor #(.\type ("n"), .gate("br")) transistor_7 (.in(1'b0), .out(transistor_7_out), .gate(1'b1));
  Transistor #(.\type ("n")) transistor_8 (.in(transistor_7_out), .out(out_7), .gate(1'b1));
  Transistor transistor_9 (.in(1'b1), .out(out_7), .gate(1'b1));
  Transistor transistor_10 (.in(1'b0), .out(out_1), .gate(1'b1));
  Transistor #(.\type ("n")) transistor_11 (.in(1'b1), .out(transistor_11_out), .gate(1'b1));
  Transistor #(.\type ("n")) transistor_12 (.in(transistor_11_out), .out(out_1), .gate(1'b1));
  Transistor transistor_13 (.in(1'b0), .out(out_1), .gate(1'b1));
  Transistor #(.gate("br")) transistor_14 (.in(1'b1), .out(out_7), .gate(1'b1));
  nand nand_1 (out_10, 1'b1, 1'b1);
  and and_1 (out_5, 1'b1, 1'b1);
  Transistor #(.gate("br")) transistor_15 (.in(1'b0), .out(out_2), .gate(1'b1));
  Transistor #(.\type ("n"), .gate("br")) transistor_16 (.in(1'b1), .out(transistor_16_out), .gate(1'b1));
  Transistor #(.\type ("n")) transistor_17 (.in(transistor_16_out), .out(out_2), .gate(1'b1));
  Transistor transistor_18 (.in(1'b0), .out(out_2), .gate(1'b1));
  Transistor #(.\type ("n"), .gate("br")) transistor_19 (.in(1'b1), .out(out_8), .gate(1'b0));
  Transistor #(.gate("br")) transistor_20 (.in(1'b0), .out(transistor_20_out), .gate(1'b0));
  Transistor transistor_21 (.in(transistor_20_out), .out(out_8), .gate(1'b1));
  Transistor #(.\type ("n")) transistor_22 (.in(1'b1), .out(out_8), .gate(1'b1));
  or or_1 (out_11, 1'b1, 1'b1);

  // Notes on the sheet:
  //   n-p-n
  //   база - затвор
  //   сток
  //   коллектор
  //   Вентиль НЕ
  //   исток
  //   эмиттер
  //   Вентиль  ИЛИ-НЕ
  //   p-n-p
  //   база - затвор
  //   сток
  //   исток
  //   Лабораторная работа №1
  //   Построение логических вентили по КМОП логике
  //   Вентиль И-НЕ
  //   Арзуманян Анна Кареновна
  //   УБВТ2403
  //   Вентиль И
  //   Вентиль ИЛИ
endmodule

module \_2_лаба  (
);

  Adder adder_1 ();  // open: a, b, out, cin, cout
  // AND_Gate and_1 is placed but not wired
  // XOR_Gate xor_1 is placed but not wired

  // Notes on the sheet:
  //   Лабораторная работа №2
  //   Построение логических вентили по КМОП логике
  //   Арзуманян Анна Кареновна
  //   УБВТ2403
endmodule
